// Logisim project alu_architecture.circ as structural Verilog: 1 circuit, main circuit main
module main (
);

  Adder adder_1 ();  // open: a, b, out, cin, cout
  Subtractor subtractor_1 ();  // open: a, b, out, bin, bout
  Multiplier multiplier_1 ();  // open: a, b, out, cin, cout
  Divider divider_1 ();  // open: a, b, out, upper, rem
endmodule
